# Fritzing sketch LightTransm (saved by Fritzing 0.9.2b)
breadboards: 1

parts:
  R4 = Resistor [tolerance=±5% resistance=1.1k package=THT]
  R5 = Resistor [tolerance=±20% resistance=110 package=THT]
  D3 = LTE-302 [package=lte-302]
  Q3 = LTR-301 [package=ltr-301]
  Composant1 = Arduino Due (Rev2b)
  Composant2 = Arduino Due (Rev2b)

nets:
  N1: R4.Pin_0, Composant2.IOREF
  N2: R4.Pin_1, Q3.C, Composant2.D2_PWM
  N3: R5.Pin_0, Composant1.GND
  N4: D3.C, Composant1.D2_PWM
  N5: Q3.E, Composant2.GND

notes:
  Ph. trans.
  IR LED
  Emitter
  Receiver
