# Fritzing sketch PIE_Balise_Cablage (saved by Fritzing 0.9.3b)

parts:
  Part1 = Arduino Uno (Rev3) - ICSP
  J1 = Piezo Speaker
  Part2 = RFID-RC522-v2

nets:
  N1: Part1.ICSP_MOSI, Part1.D11_PWM/MOSI, Part2.MOSI
  N2: Part1.D9_PWM, Part2.RST
  N3: Part1.D10_PWM/SS, Part2.SDA
  N4: Part1.D12/MISO, Part2.MISO
  N5: Part1.D13/SCK, Part2.SCK
  N6: Part1.D4, J1.pin2
  3V3: Part1.3V3, Part2.3.3V
  GND: Part1.GND, J1.pin1, Part2.GND

custom parts:
  RFID-RC522-v2: A simple China made RFID-RC522 Reader; do check the pin labels, as this is a MFRC522 based clone.
